# Fritzing sketch bt.to.ipod.dock (saved by Fritzing 0.9.2b)
circuit board: 8.46667cm x 5.64444cm
breadboards: 1

parts:
  U1 = iPod Female Connector [package=ipod_female_connector]
  Teensy_3_1 = Teensy 3.0 [part_number="Freescale ARM MK20DX128"]
  U2 = Voltage Regulator - 5V [package="TO220 [THT]"]
  50mA = Resettable Fuse PTC [package=0603]
  Part1 = Purpletooth Jamboree!!

nets:
  GND: U1.GND, Teensy_3_1.GND, U2.GND, Part1.GND
  R_OUT: U1.RIGHT_OUT, Part1.R_OUT
  L_OUT: U1.LEFT_OUT, Part1.L_OUT
  N1: U1.TX, Teensy_3_1.10
  N2: U1.RX, Teensy_3_1.9
  N3: U1.3.3V, 50mA.2
  N4: U1.FW_12V, U2.input_voltage
  VIN: Teensy_3_1.Vin, U2.output_voltage, Part1.VCC
  N5: Teensy_3_1.0, Part1.TXO
  N6: Teensy_3_1.1, Part1.RXI
  N7: Teensy_3_1.3.3V, 50mA.1
